# Fritzing sketch PIoTDistanceBreadBoardWiringDiagram (saved by Fritzing 0.9.2b)
breadboards: 1

parts:
  Raspberry_Pi1 = Raspberry Pi B rev2
  Part1 = HC-SR04
  R1 = Resistor [tolerance=±5% resistance=1k package=THT]
  R2 = Resistor [tolerance=±5% resistance=1k package=THT]
  R3 = Resistor [tolerance=±5% resistance=1k package=THT]

nets:
  5V: Raspberry_Pi1.5V, Part1.VCC
  GND: Raspberry_Pi1.GND, Part1.GND
  N1: Raspberry_Pi1.GPIO_23, Part1.Trig
  N2: Raspberry_Pi1.GPIO_24, R3.Pin_0
  N3: Part1.Echo, R1.Pin_1
  N4: R1.Pin_0, R2.Pin_1
  N5: R2.Pin_0, R3.Pin_1

notes:
  PIoT Distance Wiring Diagram
